# Fritzing sketch IR_Aufbau_Sketch (saved by Fritzing 0.9.6b)
breadboards: 1

parts:
  Arduino_UNO = Arduino Uno (Rev3)
  LCD-Display = LCD screen
  R1 = Rotary Potentiometer (Small) [maximum_resistance=10kΩ package=THT]
  RotaryEncoder = Rotary Encoder [package=THT]
  R2 = Resistor [tolerance=±5% power=0.25 resistance=220 package=THT]
  IR-LED = LTE-302 [package=lte-302]
  IR-Receiver = TSOP312.., 314.. [package=THT]
  Feedback-LED1 = LED - 5mm [color="Blue (505nm)" current=0.030 package="5 mm [THT]"]
  Feedback-LED2 = LED - 5mm [color="White (8000K)" current=0.030 package="5 mm [THT]"]
  Transistor1 = TRANSISTOR_NPN [part_number=2n2222 package=to-92-ammo]
  R3 = Resistor [tolerance=±5% power=0.25 resistance=220 package=THT]
  R4 = Resistor [tolerance=±0.25% resistance=1k package="2010 [SMD]"]
  R6 = Resistor [tolerance=±5% power=0.25 resistance=220 package=THT]
  R5 = Resistor [tolerance=±5% power=0.25 resistance=220 package=THT]

nets:
  N1: Arduino_UNO.A0, R5.Pin_0
  N2: Arduino_UNO.A1, R6.Pin_0
  N3: Arduino_UNO.D8, LCD-Display.DB5
  N4: Arduino_UNO.D9_PWM, LCD-Display.DB6
  N5: Arduino_UNO.D10_PWM/SS, LCD-Display.DB7
  N6: Arduino_UNO.D11_PWM/MOSI, IR-Receiver.Data
  N7: Arduino_UNO.D12/MISO, R4.Pin_0
  N8: Arduino_UNO.D2, RotaryEncoder.EncoderPinB
  N9: Arduino_UNO.D3_PWM, RotaryEncoder.EncoderPinC
  N10: Arduino_UNO.D4, RotaryEncoder.EncoderPinA
  N11: Arduino_UNO.D5_PWM, LCD-Display.RS
  N12: Arduino_UNO.D6_PWM, LCD-Display.E
  N13: Arduino_UNO.D7, LCD-Display.DB4
  5V: Arduino_UNO.5V, LCD-Display.VDD, R2.Pin_1, IR-LED.C, IR-Receiver.Vs
  GND: Arduino_UNO.GND, LCD-Display.VSS, LCD-Display.R/W, LCD-Display.LED-, R1.leg2, IR-Receiver.GND, Feedback-LED1.cathode, Feedback-LED2.cathode, Transistor1.E
  N14: LCD-Display.V0, R1.wiper
  N15: LCD-Display.LED+, R2.Pin_0
  N16: IR-LED.A, R3.Pin_1
  N17: Feedback-LED1.anode, R5.Pin_1
  N18: Feedback-LED2.anode, R6.Pin_1
  N19: Transistor1.B, R4.Pin_1
  N20: Transistor1.C, R3.Pin_0

notes:
  LCD-Display Helligkeits-
  dimmer
  Input
  ##Legende:##
  Rot = 5V
  Schwarz = GND
  Grau = Display
  Blau = Empfänger
  Weiß = Sender
  Orange = Dimmer
  Grün = Input (Drehschalter)
  IR Empfänger
  IR Sender
  Feedback LED's
  Blau = Empfänger
  Weiß = Sender
  GND
